// Logisim project Basic-Computer.circ as structural Verilog: 20 circuits, main circuit main
module main (
);

  wire adder_and_logic_1_e_2, clock_1_out, E, FGI, FGO, IEN, IRC, OUTRC, R, resetE, resetFGI, resetFGO,
       resetIEN, resetR, resetS, S, setIEN, setR, TRC;
  wire [1:0] DRC, RAMC;
  wire [2:0] ACC, ARC, Bus_slct, PCC;
  wire [3:0] T;
  wire [7:0] cpu_controller_1_aluc, n8bit_register_1_out_5, n8bit_register_2_out_5;
  wire [15:0] AC, adder_and_logic_1_ac_2, AR_out_6, bus_1_out_11, DR, IR, PC_out_6, ram_1_data, TR_out_6;

  Clock clock_1 (.out(clock_1_out));
  CPU_controller cpu_controller_1 (
    .R(R), .DR(DR), .AC(AC), .E(E), .FGI(FGI), .FGO(FGO), .IR(IR), .incSC(S), .ARC(ARC), .PCC(PCC),
    .DRC(DRC), .ACC(ACC), .IRC(IRC), .TRC(TRC), .OUTRC(OUTRC), .Clk(clock_1_out), .memory(RAMC), .IEN(IEN),
    .FFC({resetFGO, resetFGI, resetIEN, setIEN, resetR, setR, resetS, resetE}), .ALUC(cpu_controller_1_aluc),
    .bus_slct(Bus_slct));
  J_K_Flip_Flop u_S (.clk(clock_1_out), .Q(S), .preset(1'b1), .reset(resetS));  // open: J, K, Qn, en
  // Probe on resetS
  J_K_Flip_Flop u_R (.J(setR), .clk(clock_1_out), .K(resetR), .Q(R));  // open: Qn, preset, en, reset
  J_K_Flip_Flop u_IEN (.J(setIEN), .clk(clock_1_out), .K(resetIEN), .Q(IEN));  // open: Qn, preset, en, reset
  J_K_Flip_Flop u_FGI (.J(1'b0), .clk(clock_1_out), .K(resetFGI), .Q(FGI));  // open: Qn, preset, en, reset
  J_K_Flip_Flop u_FGO (.J(1'b0), .clk(clock_1_out), .K(resetFGO), .Q(FGO));  // open: Qn, preset, en, reset
  // Probe on adder_and_logic_1_ac_2
  // Probe on cpu_controller_1_aluc
  adder_and_logic adder_and_logic_1 (
    .AC(AC), .DR(DR), .E(E), .INPR(n8bit_register_1_out_5), .\and (cpu_controller_1_aluc[0]),
    .add(cpu_controller_1_aluc[1]), .transfer_dr(cpu_controller_1_aluc[2]), .cma(cpu_controller_1_aluc[3]),
    .cir(cpu_controller_1_aluc[4]), .cil(cpu_controller_1_aluc[5]), .inpr_2(cpu_controller_1_aluc[6]),
    .E_2(adder_and_logic_1_e_2), .AC_2(adder_and_logic_1_ac_2), .cme(cpu_controller_1_aluc[7]));
  // Probe on DRC
  // Probe on ACC
  // Probe on IRC
  // Probe on RAMC
  // Probe on ARC
  // Probe on PCC
  D_Flip_Flop u_E (.clk(clock_1_out), .D(adder_and_logic_1_e_2), .Q(E), .reset(resetE));  // open: Qn, preset, en
  _8bit_register u_8bit_register_1 (
    .ld(1'b1), .clk(clock_1_out), .out_5(n8bit_register_1_out_5), .clr(1'b0));  // open: in_1
  _8bit_register u_8bit_register_2 (
    .in_1(bus_1_out_11), .ld(OUTRC), .clk(clock_1_out), .out_5(n8bit_register_2_out_5), .clr(1'b0));
  RAM #(.addrWidth(12), .dataWidth(16), .bus("separate")) ram_1 (
    .addr(AR_out_6[11:0]), .din(bus_1_out_11), .data(ram_1_data), .str(RAMC[1]), .clk(clock_1_out),
    .ld(RAMC[0]));  // open: sel, clr
  _12bit_register AR (
    .ld(ARC[2]), .inc(ARC[1]), .clr(ARC[0]), .clk(clock_1_out), .out_6(AR_out_6), .in_1(bus_1_out_11));
  _12bit_register PC (
    .ld(PCC[2]), .inc(PCC[1]), .clr(PCC[0]), .clk(clock_1_out), .out_6(PC_out_6), .in_1(bus_1_out_11));
  register u_DR (.in_1(bus_1_out_11), .load(DRC[1]), .inc(DRC[0]), .out_6(DR), .clr(1'b0), .in_5(clock_1_out));
  register u_AC (
    .in_1(adder_and_logic_1_ac_2), .load(ACC[2]), .inc(ACC[1]), .out_6(AC), .clr(ACC[0]), .in_5(clock_1_out));
  register u_IR (.in_1(bus_1_out_11), .load(IRC), .inc(1'b0), .out_6(IR), .clr(1'b0), .in_5(clock_1_out));
  register TR (.in_1(bus_1_out_11), .load(TRC), .inc(1'b0), .out_6(TR_out_6), .clr(1'b0), .in_5(clock_1_out));
  // Probe on n8bit_register_2_out_5
  // Probe on T
  // Probe on ram_1_data
  // Probe on AR_out_6
  // Probe on PC_out_6
  // Probe on DR
  // Probe on AC
  // Probe on IR
  // Probe on TR_out_6
  // Probe on Bus_slct
  bus bus_1 (
    .in_1(AR_out_6), .in_2(PC_out_6), .in_4(AC), .in_5(IR), .in_6(TR_out_6), .in_7(ram_1_data),
    .s0(Bus_slct[2]), .s1(Bus_slct[1]), .s2(Bus_slct[0]), .out_11(bus_1_out_11), .in_3(DR));
  // Probe on bus_1_out_11

  // Notes on the sheet:
  //   OUTR
  //   INPR
endmodule

module bus (
  input  [15:0] in_1,
  input  [15:0] in_2,
  input  [15:0] in_3,
  input  [15:0] in_4,
  input  [15:0] in_5,
  input  [15:0] in_6,
  input  [15:0] in_7,
  input  s0,
  input  s1,
  input  s2,
  output [15:0] out_11
);

  Multiplexer #(.select(3), .width(16)) multiplexer_1 (
    .in0({16{1'b1}}), .in1(in_1), .in2(in_2), .in3(in_3), .in4(in_4), .in5(in_5), .in6(in_6), .in7(in_7),
    .out(out_11), .sel({s2, s1, s0}), .en(1'b1));
endmodule

module register (
  input  [15:0] in_1,
  input  load,
  input  inc,
  input  clr,
  input  in_5,
  output [15:0] out_6
);

  wire n16bit_adder_1_cout;
  wire [15:0] multiplexer_1_out, n16bit_adder_1_s;

  _16bit_adder u_16bit_adder_1 (.A(out_6), .B(16'h1), .Cout(n16bit_adder_1_cout), .S(n16bit_adder_1_s), .Cin(1'b0));
  Multiplexer #(.select(2), .width(16)) multiplexer_1 (
    .in0(out_6), .in1(in_1), .in2(n16bit_adder_1_s), .in3(out_6), .out(multiplexer_1_out), .sel({inc, load}));  // open: en
  Register #(.width(16)) register_1 (.D(multiplexer_1_out), .en(1'b1), .Q(out_6), .clk(in_5), .clr(clr));
endmodule

module half_adder (
  input  in_1,
  input  in_2,
  output out_3,
  output out_4
);

  xor xor_1 (out_3, in_1, in_2);
  and and_1 (out_4, in_1, in_2);
endmodule

module full_adder (
  input  in_1,
  input  in_2,
  input  in_3,
  output out_4,
  output out_5
);

  wire half_adder_1_out_3, half_adder_1_out_4, half_adder_2_out_4;

  half_adder half_adder_1 (.in_1(in_2), .in_2(in_3), .out_3(half_adder_1_out_3), .out_4(half_adder_1_out_4));
  half_adder half_adder_2 (.in_1(in_1), .in_2(half_adder_1_out_3), .out_3(out_4), .out_4(half_adder_2_out_4));
  or or_1 (out_5, half_adder_2_out_4, half_adder_1_out_4);
endmodule

module _12bit_register (
  input  [15:0] in_1,
  input  ld,
  input  inc,
  input  clr,
  input  clk,
  output [15:0] out_6
);

  wire n12bit_adder_1_cout;
  wire [11:0] multiplexer_1_out, n12bit_adder_1_s;

  _12bit_adder u_12bit_adder_1 (
    .A(out_6[11:0]), .B(12'h1), .Cout(n12bit_adder_1_cout), .S(n12bit_adder_1_s), .Cin(1'b0));
  Multiplexer #(.select(2), .width(12)) multiplexer_1 (
    .in0(out_6[11:0]), .in1(in_1[11:0]), .in2(n12bit_adder_1_s), .in3(out_6[11:0]), .out(multiplexer_1_out),
    .sel({inc, ld}));  // open: en
  Register #(.width(12)) register_1 (.D(multiplexer_1_out), .en(1'b1), .Q(out_6[11:0]), .clk(clk), .clr(clr));

  assign out_6[15:12] = 4'b0000;
endmodule

module adder_and_logic (
  input  [15:0] AC,
  input  [15:0] DR,
  input  E,
  input  [7:0] INPR,
  input  \and ,
  input  add,
  input  transfer_dr,
  input  cma,
  input  cir,
  input  cil,
  input  inpr_2,
  input  cme,
  output E_2,
  output [15:0] AC_2
);

  wire adder_1_cout, not_2_out;
  wire [2:0] priority_encoder_1_out;
  wire [15:0] adder_1_out, and_1_out, not_1_out;

  assign and_1_out = AC & DR;  // AND_Gate and_1, 16 bits wide
  Adder #(.width(16)) adder_1 (.a(AC), .b(DR), .out(adder_1_out), .cin(1'b0), .cout(adder_1_cout));
  assign not_1_out = ~AC;  // NOT_Gate not_1, 16 bits wide
  Priority_Encoder priority_encoder_1 (
    .in0(\and ), .in1(add), .in2(transfer_dr), .in3(cma), .in4(cir), .in5(cil), .in6(inpr_2), .in7(cme),
    .out(priority_encoder_1_out));  // open: en_in, gs, en_out
  Multiplexer #(.select(3), .width(16)) multiplexer_1 (
    .in0(and_1_out), .in1(adder_1_out), .in2(DR), .in3(not_1_out), .in4({E, AC[15:1]}), .in5({AC[14:0], E}),
    .in6({{8{1'b0}}, INPR}), .in7(AC), .out(AC_2), .sel(priority_encoder_1_out), .en(1'b1));
  not not_2 (not_2_out, E);
  Multiplexer #(.select(3)) multiplexer_2 (
    .in0(E), .in1(adder_1_cout), .in2(E), .in3(E), .in4(AC[0]), .in5(AC[15]), .in6(E), .in7(not_2_out),
    .out(E_2), .sel(priority_encoder_1_out), .en(1'b1));
endmodule

module _8bit_register (
  input  [15:0] in_1,
  input  ld,
  input  clk,
  input  clr,
  output [7:0] out_5
);

  wire [7:0] multiplexer_1_out;

  Multiplexer #(.width(8)) multiplexer_1 (.in0(out_5), .in1(in_1[7:0]), .out(multiplexer_1_out), .sel(ld), .en(1'b1));
  Register register_1 (.D(multiplexer_1_out), .Q(out_5), .clk(clk), .clr(clr));  // open: en
endmodule

module CPU_controller (
  input  R,
  input  [15:0] DR,
  input  [15:0] AC,
  input  E,
  input  FGI,
  input  FGO,
  input  [15:0] IR,
  input  incSC,
  input  Clk,
  input  IEN,
  output [2:0] ARC,
  output [2:0] PCC,
  output [1:0] DRC,
  output [2:0] ACC,
  output IRC,
  output TRC,
  output OUTRC,
  output [1:0] memory,
  output [7:0] FFC,
  output [7:0] ALUC,
  output [2:0] bus_slct
);

  wire and_3_out, D7, d_ff_1_q, I_q, not_1_out, resetS, sc_controller_1_clr, T0, T1, T3;
  wire [3:0] SC_q;
  wire [6:0] decoder_1_out0;
  wire [15:2] decoder_2_out2;

  SC_controller sc_controller_1 (
    .D0_D7({D7, decoder_1_out0}), .T0_T15({decoder_2_out2[15:4], T3, decoder_2_out2[2], T1, T0}), .I(I_q),
    .R(R), .CLR(sc_controller_1_clr));
  Counter #(.width(4), .max('hf), .ongoal("load")) SC (
    .count(incSC), .Q(SC_q), .clk(Clk), .clr(d_ff_1_q));  // open: load, D, carry
  D_Flip_Flop d_ff_1 (.clk(Clk), .D(sc_controller_1_clr), .Q(d_ff_1_q));  // open: Qn, preset, en, reset
  D_Flip_Flop perv_resetS_signal (.clk(Clk), .D(FFC[1]), .Q(resetS));  // open: Qn, preset, en, reset
  Decoder #(.select(3)) decoder_1 (
    .out0(decoder_1_out0[0]), .out1(decoder_1_out0[1]), .out2(decoder_1_out0[2]), .out3(decoder_1_out0[3]),
    .out4(decoder_1_out0[4]), .out5(decoder_1_out0[5]), .out6(decoder_1_out0[6]), .out7(D7), .sel(IR[14:12]));  // open: en
  D_Flip_Flop I (.clk(Clk), .D(IR[15]), .Q(I_q));  // open: Qn, preset, en, reset
  Decoder #(.select(4)) decoder_2 (
    .out0(T0), .out1(T1), .out2(decoder_2_out2[2]), .out3(T3), .out4(decoder_2_out2[4]),
    .out5(decoder_2_out2[5]), .out6(decoder_2_out2[6]), .out7(decoder_2_out2[7]), .out8(decoder_2_out2[8]),
    .out9(decoder_2_out2[9]), .out10(decoder_2_out2[10]), .out11(decoder_2_out2[11]),
    .out12(decoder_2_out2[12]), .out13(decoder_2_out2[13]), .out14(decoder_2_out2[14]),
    .out15(decoder_2_out2[15]), .sel(SC_q));  // open: en
  AR_controller ar_controller_1 (
    .D0_D7({D7, decoder_1_out0}), .I(I_q), .R(R), .LD(ARC[2]), .INC(ARC[1]), .CLR(ARC[0]),
    .T0_T15({decoder_2_out2[15:4], T3, decoder_2_out2[2], T1, T0}));
  not not_1 (not_1_out, R);
  RAM_controller ram_controller_1 (
    .R(R), .D0_D7({D7, decoder_1_out0}), .T0_T15({decoder_2_out2[15:4], T3, decoder_2_out2[2], T1, T0}),
    .I(I_q), .write(memory[1]), .read(memory[0]));
  PC_controller pc_controller_1 (
    .D0_D7({D7, decoder_1_out0}), .T0_T15({decoder_2_out2[15:4], T3, decoder_2_out2[2], T1, T0}),
    .IR0_11(IR[11:0]), .E(E), .FGI(FGI), .FGO(FGO), .R(R), .DR(DR), .I(I_q), .AC(AC), .LD(PCC[2]),
    .INC(PCC[1]), .CLR(PCC[0]));
  DR_controller dr_controller_1 (
    .D0_D7({D7, decoder_1_out0}), .LD(DRC[1]),
    .T0_T15({decoder_2_out2[15:4], T3, decoder_2_out2[2], T1, T0}), .INC(DRC[0]));
  AC_controller ac_controller_1 (
    .D0_D7({D7, decoder_1_out0}), .T0_T15({decoder_2_out2[15:4], T3, decoder_2_out2[2], T1, T0}), .I(I_q),
    .LD(ACC[2]), .INC(ACC[1]), .CLR(ACC[0]), .IR0_11(IR[11:0]));
  and and_1 (IRC, T1, not_1_out);
  and and_2 (TRC, T0, R);
  and and_3 (and_3_out, D7, I_q, T3);
  flipflops_controller flipflops_controller_1 (
    .D0_D7({D7, decoder_1_out0}), .T0_T15({decoder_2_out2[15:4], T3, decoder_2_out2[2], T1, T0}), .IEN(IEN),
    .FGI(FGI), .FGO(FGO), .IR0_11(IR[11:0]), .R(R), .I(I_q), .reset_E(FFC[0]), .reset_S(FFC[1]),
    .set_R(FFC[2]), .reset_R(FFC[3]), .set_IEN(FFC[4]), .reset_IEN(FFC[5]), .reset_FGI(FFC[6]),
    .reset_FGO(FFC[7]), .S(resetS));
  AddLog_controller addlog_controller_1 (
    .D0_D7({D7, decoder_1_out0}), .T0_T15({decoder_2_out2[15:4], T3, decoder_2_out2[2], T1, T0}),
    .IR0_11(IR[11:0]), .I(I_q), .\and (ALUC[0]), .add(ALUC[1]), .transfer_DR(ALUC[2]), .CMA(ALUC[3]),
    .CIR(ALUC[4]), .CIL(ALUC[5]), .INPR(ALUC[6]), .CME(ALUC[7]));
  bus_controller bus_controller_1 (
    .D0_D7({D7, decoder_1_out0}), .T0_T15({decoder_2_out2[15:4], T3, decoder_2_out2[2], T1, T0}),
    .IR0_11(IR[11:0]), .R(R), .I(I_q), .s0(bus_slct[2]), .s1(bus_slct[1]), .s2(bus_slct[0]));
  and and_4 (OUTRC, and_3_out, IR[10]);

  // Other names for the same wires on the sheet: B10 = IR[10]; s = FFC[1]
endmodule

module AR_controller (
  input  [7:0] D0_D7,
  input  I,
  input  R,
  input  [15:0] T0_T15,
  output LD,
  output INC,
  output CLR
);

  wire and_1_out, and_2_out, and_3_out, not_1_out, not_2_out;

  not not_1 (not_1_out, D0_D7[7]);
  not not_2 (not_2_out, R);
  and and_1 (and_1_out, not_1_out, I, T0_T15[3]);
  and and_2 (and_2_out, T0_T15[2], not_2_out);
  and and_3 (and_3_out, not_2_out, T0_T15[0]);
  and and_4 (INC, T0_T15[4], D0_D7[5]);
  and and_5 (CLR, R, T0_T15[0]);
  or or_1 (LD, and_1_out, and_2_out, and_3_out);

  // Other names for the same wires on the sheet: D0 = D0_D7[0]; D1 = D0_D7[1]; D2 = D0_D7[2]; D3 = D0_D7[3];
  //   D4 = D0_D7[4]; D5 = D0_D7[5]; D6 = D0_D7[6]; D7 = D0_D7[7]; T0 = T0_T15[0]; T1 = T0_T15[1]; T2 = T0_T15[2];
  //   T3 = T0_T15[3]; T4 = T0_T15[4]; T5 = T0_T15[5]; T6 = T0_T15[6]
endmodule

module PC_controller (
  input  [7:0] D0_D7,
  input  [15:0] T0_T15,
  input  [11:0] IR0_11,
  input  E,
  input  FGI,
  input  FGO,
  input  R,
  input  [15:0] DR,
  input  I,
  input  [15:0] AC,
  output LD,
  output INC,
  output CLR
);

  wire ACZ, and_3_out, and_4_out, and_5_out, and_6_out, and_7_out, and_8_out, and_9_out, and_10_out,
       and_11_out, and_12_out, and_13_out, DRZ, not_1_out, not_2_out, not_3_out, not_4_out, p, r_t;

  not not_1 (not_1_out, I);
  and and_1 (r_t, D0_D7[7], not_1_out, T0_T15[3]);
  and and_2 (p, D0_D7[7], I, T0_T15[3]);
  not not_2 (not_2_out, R);
  not not_3 (not_3_out, AC[15]);
  not not_4 (not_4_out, E);
  and and_3 (and_3_out, T0_T15[4], D0_D7[4]);
  and and_4 (and_4_out, T0_T15[5], D0_D7[5]);
  and and_5 (and_5_out, not_2_out, T0_T15[1]);
  and and_6 (and_6_out, R, T0_T15[2]);
  and and_7 (and_7_out, T0_T15[6], D0_D7[6], DRZ);
  and and_8 (and_8_out, r_t, IR0_11[4], not_3_out);
  and and_9 (and_9_out, r_t, IR0_11[3], AC[15]);
  and and_10 (and_10_out, r_t, IR0_11[2], ACZ);
  and and_11 (and_11_out, r_t, IR0_11[1], not_4_out);
  and and_12 (and_12_out, p, IR0_11[9], FGI);
  and and_13 (and_13_out, p, IR0_11[8], FGO);
  and and_14 (CLR, R, T0_T15[1]);
  nor nor_1 (DRZ, DR[15], DR[14], DR[13], DR[12], DR[11], DR[10], DR[9], DR[8], DR[6], DR[5], DR[4], DR[3], DR[2], DR[1], DR[0], DR[7]);
  nor nor_2 (ACZ, AC[15], AC[14], AC[13], AC[12], AC[11], AC[10], AC[9], AC[8], AC[6], AC[5], AC[4], AC[3], AC[2], AC[1], AC[0], AC[7]);
  or or_1 (LD, and_3_out, and_4_out);
  or or_2 (INC, and_5_out, and_6_out, and_7_out, and_8_out, and_9_out, and_10_out, and_11_out, and_12_out, and_13_out);

  // Other names for the same wires on the sheet: D0 = D0_D7[0]; D1 = D0_D7[1]; D2 = D0_D7[2]; D3 = D0_D7[3];
  //   D4 = D0_D7[4]; D5 = D0_D7[5]; D6 = D0_D7[6]; D7 = D0_D7[7]; B0 = IR0_11[0]; B1 = IR0_11[1]; B2 = IR0_11[2];
  //   B3 = IR0_11[3]; B4 = IR0_11[4]; B5 = IR0_11[5]; B6 = IR0_11[6]; B7 = IR0_11[7]; B8 = IR0_11[8]; B9 = IR0_11[9];
  //   B10 = IR0_11[10]; B11 = IR0_11[11]; T0 = T0_T15[0]; T1 = T0_T15[1]; T2 = T0_T15[2]; T3 = T0_T15[3];
  //   T4 = T0_T15[4]; T5 = T0_T15[5]; T6 = T0_T15[6]
endmodule

module DR_controller (
  input  [7:0] D0_D7,
  input  [15:0] T0_T15,
  output LD,
  output INC
);

  wire and_1_out, and_2_out, and_3_out, and_4_out;

  and and_1 (and_1_out, T0_T15[4], D0_D7[0]);
  and and_2 (and_2_out, T0_T15[4], D0_D7[1]);
  and and_3 (and_3_out, T0_T15[4], D0_D7[2]);
  and and_4 (and_4_out, T0_T15[4], D0_D7[6]);
  and and_5 (INC, T0_T15[5], D0_D7[6]);
  or or_1 (LD, and_1_out, and_2_out, and_3_out, and_4_out);

  // Other names for the same wires on the sheet: D0 = D0_D7[0]; D1 = D0_D7[1]; D2 = D0_D7[2]; D3 = D0_D7[3];
  //   D4 = D0_D7[4]; D5 = D0_D7[5]; D6 = D0_D7[6]; D7 = D0_D7[7]; T0 = T0_T15[0]; T1 = T0_T15[1]; T2 = T0_T15[2];
  //   T3 = T0_T15[3]; T4 = T0_T15[4]; T5 = T0_T15[5]; T6 = T0_T15[6]
endmodule

module AC_controller (
  input  [7:0] D0_D7,
  input  [15:0] T0_T15,
  input  [11:0] IR0_11,
  input  I,
  output LD,
  output INC,
  output CLR
);

  wire and_3_out, and_4_out, and_5_out, and_6_out, and_7_out, and_8_out, and_9_out, not_1_out, p, r;

  not not_1 (not_1_out, I);
  and and_1 (r, D0_D7[7], not_1_out, T0_T15[3]);
  and and_2 (p, D0_D7[7], I, T0_T15[3]);
  and and_3 (and_3_out, T0_T15[5], D0_D7[0]);
  and and_4 (and_4_out, T0_T15[5], D0_D7[1]);
  and and_5 (and_5_out, T0_T15[5], D0_D7[2]);
  and and_6 (and_6_out, r, IR0_11[6]);
  and and_7 (and_7_out, r, IR0_11[7]);
  and and_8 (and_8_out, r, IR0_11[9]);
  and and_9 (and_9_out, p, IR0_11[11]);
  and and_10 (INC, r, IR0_11[5]);
  and and_11 (CLR, r, IR0_11[11]);
  or or_1 (LD, and_3_out, and_4_out, and_5_out, and_6_out, and_7_out, and_8_out, and_9_out);

  // Other names for the same wires on the sheet: D0 = D0_D7[0]; D1 = D0_D7[1]; D2 = D0_D7[2]; D3 = D0_D7[3];
  //   D4 = D0_D7[4]; D5 = D0_D7[5]; D6 = D0_D7[6]; D7 = D0_D7[7]; B0 = IR0_11[0]; B1 = IR0_11[1]; B2 = IR0_11[2];
  //   B3 = IR0_11[3]; B4 = IR0_11[4]; B5 = IR0_11[5]; B6 = IR0_11[6]; B7 = IR0_11[7]; B8 = IR0_11[8]; B9 = IR0_11[9];
  //   B10 = IR0_11[10]; B11 = IR0_11[11]; T0 = T0_T15[0]; T1 = T0_T15[1]; T2 = T0_T15[2]; T3 = T0_T15[3];
  //   T4 = T0_T15[4]; T5 = T0_T15[5]; T6 = T0_T15[6]
endmodule

module SC_controller (
  input  [7:0] D0_D7,
  input  [15:0] T0_T15,
  input  I,
  input  R,
  output CLR
);

  wire and_1_out, and_2_out, and_3_out, and_4_out, and_5_out, and_6_out, and_7_out, and_8_out, and_9_out,
       and_10_out, not_1_out;

  not not_1 (not_1_out, I);
  and and_1 (and_1_out, D0_D7[7], not_1_out, T0_T15[3]);
  and and_2 (and_2_out, D0_D7[7], I, T0_T15[3]);
  and and_3 (and_3_out, D0_D7[0], T0_T15[5]);
  and and_4 (and_4_out, D0_D7[1], T0_T15[5]);
  and and_5 (and_5_out, D0_D7[2], T0_T15[5]);
  and and_6 (and_6_out, D0_D7[3], T0_T15[4]);
  and and_7 (and_7_out, D0_D7[4], T0_T15[4]);
  and and_8 (and_8_out, D0_D7[5], T0_T15[5]);
  and and_9 (and_9_out, D0_D7[6], T0_T15[6]);
  and and_10 (and_10_out, R, T0_T15[2]);
  or or_1 (CLR, and_3_out, and_4_out, and_5_out, and_6_out, and_7_out, and_8_out, and_9_out, and_1_out, and_2_out, and_10_out);

  // Other names for the same wires on the sheet: D0 = D0_D7[0]; D1 = D0_D7[1]; D2 = D0_D7[2]; D3 = D0_D7[3];
  //   D4 = D0_D7[4]; D5 = D0_D7[5]; D6 = D0_D7[6]; D7 = D0_D7[7]; T0 = T0_T15[0]; T1 = T0_T15[1]; T2 = T0_T15[2];
  //   T3 = T0_T15[3]; T4 = T0_T15[4]; T5 = T0_T15[5]; T6 = T0_T15[6]; T7 = T0_T15[7]
endmodule

module RAM_controller (
  input  R,
  input  [7:0] D0_D7,
  input  [15:0] T0_T15,
  input  I,
  output write,
  output read
);

  wire and_1_out, and_2_out, and_3_out, and_4_out, and_5_out, and_6_out, and_7_out, and_8_out, and_9_out,
       and_10_out, not_1_out, not_2_out;

  not not_1 (not_1_out, R);
  not not_2 (not_2_out, D0_D7[7]);
  and and_1 (and_1_out, R, T0_T15[1]);
  and and_2 (and_2_out, D0_D7[3], T0_T15[4]);
  and and_3 (and_3_out, D0_D7[5], T0_T15[4]);
  and and_4 (and_4_out, D0_D7[6], T0_T15[6]);
  and and_5 (and_5_out, not_2_out, I, T0_T15[3]);
  and and_6 (and_6_out, not_1_out, T0_T15[1]);
  and and_7 (and_7_out, D0_D7[0], T0_T15[4]);
  and and_8 (and_8_out, D0_D7[1], T0_T15[4]);
  and and_9 (and_9_out, D0_D7[2], T0_T15[4]);
  and and_10 (and_10_out, D0_D7[6], T0_T15[4]);
  or or_1 (write, and_1_out, and_2_out, and_3_out, and_4_out);
  or or_2 (read, and_5_out, and_6_out, and_7_out, and_8_out, and_9_out, and_10_out);

  // Other names for the same wires on the sheet: D0 = D0_D7[0]; D1 = D0_D7[1]; D2 = D0_D7[2]; D3 = D0_D7[3];
  //   D4 = D0_D7[4]; D5 = D0_D7[5]; D6 = D0_D7[6]; D7 = D0_D7[7]; T0 = T0_T15[0]; T1 = T0_T15[1]; T2 = T0_T15[2];
  //   T3 = T0_T15[3]; T4 = T0_T15[4]; T5 = T0_T15[5]; T6 = T0_T15[6]
endmodule

module flipflops_controller (
  input  [7:0] D0_D7,
  input  S,
  input  [15:0] T0_T15,
  input  IEN,
  input  FGI,
  input  FGO,
  input  [11:0] IR0_11,
  input  R,
  input  I,
  output reset_E,
  output reset_S,
  output set_R,
  output reset_R,
  output set_IEN,
  output reset_IEN,
  output reset_FGI,
  output reset_FGO
);

  wire and_6_out, and_9_out, nor_1_out, not_1_out, or_1_out, p, r_t, undriven;

  not not_1 (not_1_out, I);
  and and_1 (r_t, D0_D7[7], not_1_out, T0_T15[3]);
  and and_2 (p, D0_D7[7], I, T0_T15[3]);
  and and_3 (reset_E, IR0_11[10], r_t);
  nor nor_1 (nor_1_out, T0_T15[0], T0_T15[1], T0_T15[2]);
  or or_1 (or_1_out, FGI, undriven);
  and and_4 (reset_R, T0_T15[2], R);
  and and_5 (set_IEN, p, IR0_11[7]);
  and and_6 (and_6_out, p, IR0_11[6]);
  and and_7 (reset_FGI, p, IR0_11[11]);
  and and_8 (reset_FGO, p, IR0_11[10]);
  and and_9 (and_9_out, IR0_11[0], r_t);
  or or_2 (reset_IEN, reset_R, and_6_out);
  or or_3 (reset_S, and_9_out, S);
  and and_10 (set_R, nor_1_out, IEN, or_1_out);

  // Other names for the same wires on the sheet: D0 = D0_D7[0]; D1 = D0_D7[1]; D2 = D0_D7[2]; D3 = D0_D7[3];
  //   D4 = D0_D7[4]; D5 = D0_D7[5]; D6 = D0_D7[6]; D7 = D0_D7[7]; B0 = IR0_11[0]; B1 = IR0_11[1]; B2 = IR0_11[2];
  //   B3 = IR0_11[3]; B4 = IR0_11[4]; B5 = IR0_11[5]; B6 = IR0_11[6]; B7 = IR0_11[7]; B8 = IR0_11[8]; B9 = IR0_11[9];
  //   B10 = IR0_11[10]; B11 = IR0_11[11]; T0 = T0_T15[0]; T1 = T0_T15[1]; T2 = T0_T15[2]; T3 = T0_T15[3];
  //   T4 = T0_T15[4]; T5 = T0_T15[5]; T6 = T0_T15[6]
endmodule

module AddLog_controller (
  input  [7:0] D0_D7,
  input  [15:0] T0_T15,
  input  [11:0] IR0_11,
  input  I,
  output \and ,
  output add,
  output transfer_DR,
  output CMA,
  output CIR,
  output CIL,
  output INPR,
  output CME
);

  wire not_1_out, p, r;

  not not_1 (not_1_out, I);
  and and_1 (\and , D0_D7[0], T0_T15[5]);
  and and_2 (add, D0_D7[1], T0_T15[5]);
  and and_3 (transfer_DR, D0_D7[2], T0_T15[5]);
  and and_4 (CMA, r, IR0_11[9]);
  and and_5 (CIR, r, IR0_11[7]);
  and and_6 (CIL, r, IR0_11[6]);
  and and_7 (INPR, p, IR0_11[11]);
  and and_8 (CME, r, IR0_11[8]);
  and and_9 (r, D0_D7[7], not_1_out, T0_T15[3]);
  and and_10 (p, D0_D7[7], I, T0_T15[3]);

  // Other names for the same wires on the sheet: D0 = D0_D7[0]; D1 = D0_D7[1]; D2 = D0_D7[2]; D3 = D0_D7[3];
  //   D4 = D0_D7[4]; D5 = D0_D7[5]; D6 = D0_D7[6]; D7 = D0_D7[7]; B0 = IR0_11[0]; B1 = IR0_11[1]; B2 = IR0_11[2];
  //   B3 = IR0_11[3]; B4 = IR0_11[4]; B5 = IR0_11[5]; B6 = IR0_11[6]; B7 = IR0_11[7]; B8 = IR0_11[8]; B9 = IR0_11[9];
  //   B10 = IR0_11[10]; B11 = IR0_11[11]; T0 = T0_T15[0]; T1 = T0_T15[1]; T2 = T0_T15[2]; T3 = T0_T15[3];
  //   T4 = T0_T15[4]; T5 = T0_T15[5]; T6 = T0_T15[6]
endmodule

module bus_controller (
  input  [7:0] D0_D7,
  input  [15:0] T0_T15,
  input  [11:0] IR0_11,
  input  R,
  input  I,
  output s0,
  output s1,
  output s2
);

  wire AC, and_3_out, and_4_out, and_5_out, and_7_out, and_8_out, and_11_out, and_12_out, and_13_out,
       and_14_out, and_15_out, and_16_out, AR, DR, IR, not_1_out, not_2_out, not_3_out, p, PC, r_t, RAM, TR;

  not not_1 (not_1_out, I);
  and and_1 (r_t, D0_D7[7], not_1_out, T0_T15[3]);
  and and_2 (p, D0_D7[7], I, T0_T15[3]);
  not not_2 (not_2_out, R);
  and and_3 (and_3_out, D0_D7[4], T0_T15[4]);
  and and_4 (and_4_out, D0_D7[5], T0_T15[5]);
  and and_5 (and_5_out, D0_D7[5], T0_T15[4]);
  and and_6 (DR, D0_D7[6], T0_T15[6]);
  and and_7 (and_7_out, D0_D7[3], T0_T15[4]);
  and and_8 (and_8_out, p, IR0_11[10]);
  not not_3 (not_3_out, D0_D7[7]);
  and and_9 (IR, not_2_out, T0_T15[2]);
  and and_10 (TR, R, T0_T15[1]);
  and and_11 (and_11_out, not_2_out, T0_T15[1]);
  and and_12 (and_12_out, not_3_out, I, T0_T15[3]);
  and and_13 (and_13_out, D0_D7[0], T0_T15[4]);
  and and_14 (and_14_out, D0_D7[1], T0_T15[4]);
  and and_15 (and_15_out, D0_D7[2], T0_T15[4]);
  and and_16 (and_16_out, D0_D7[6], T0_T15[4]);
  or or_1 (AR, and_3_out, and_4_out);
  or or_2 (PC, T0_T15[0], and_5_out);
  or or_3 (AC, and_7_out, and_8_out);
  or or_4 (RAM, and_11_out, and_12_out, and_13_out, and_14_out, and_15_out, and_16_out);
  or or_5 (s0, AR, DR, IR, RAM);
  or or_6 (s1, PC, DR, TR, RAM);
  or or_7 (s2, AC, TR, IR, RAM);

  // Other names for the same wires on the sheet: D0 = D0_D7[0]; D1 = D0_D7[1]; D2 = D0_D7[2]; D3 = D0_D7[3];
  //   D4 = D0_D7[4]; D5 = D0_D7[5]; D6 = D0_D7[6]; D7 = D0_D7[7]; B0 = IR0_11[0]; B1 = IR0_11[1]; B2 = IR0_11[2];
  //   B3 = IR0_11[3]; B4 = IR0_11[4]; B5 = IR0_11[5]; B6 = IR0_11[6]; B7 = IR0_11[7]; B8 = IR0_11[8]; B9 = IR0_11[9];
  //   B10 = IR0_11[10]; B11 = IR0_11[11]; T0 = T0_T15[0]; T1 = T0_T15[1]; T2 = T0_T15[2]; T3 = T0_T15[3];
  //   T4 = T0_T15[4]; T5 = T0_T15[5]; T6 = T0_T15[6]
endmodule

module _12bit_adder (
  input  [11:0] A,
  input  Cin,
  input  [11:0] B,
  output Cout,
  output [11:0] S
);

  wire full_adder_1_out_5, full_adder_2_out_5, full_adder_3_out_5, full_adder_4_out_5, full_adder_5_out_5,
       full_adder_6_out_5, full_adder_7_out_5, full_adder_8_out_5, full_adder_9_out_5, full_adder_10_out_5,
       full_adder_11_out_5;

  full_adder full_adder_1 (.in_1(Cin), .in_2(A[0]), .in_3(B[0]), .out_4(S[0]), .out_5(full_adder_1_out_5));
  full_adder full_adder_2 (
    .in_1(full_adder_1_out_5), .in_2(A[1]), .in_3(B[1]), .out_4(S[1]), .out_5(full_adder_2_out_5));
  full_adder full_adder_3 (
    .in_1(full_adder_2_out_5), .in_2(A[2]), .in_3(B[2]), .out_4(S[2]), .out_5(full_adder_3_out_5));
  full_adder full_adder_4 (
    .in_1(full_adder_3_out_5), .in_2(A[3]), .in_3(B[3]), .out_4(S[3]), .out_5(full_adder_4_out_5));
  full_adder full_adder_5 (
    .in_1(full_adder_4_out_5), .in_2(A[4]), .in_3(B[4]), .out_4(S[4]), .out_5(full_adder_5_out_5));
  full_adder full_adder_6 (
    .in_1(full_adder_5_out_5), .in_2(A[5]), .in_3(B[5]), .out_4(S[5]), .out_5(full_adder_6_out_5));
  full_adder full_adder_7 (
    .in_1(full_adder_6_out_5), .in_2(A[6]), .in_3(B[6]), .out_4(S[6]), .out_5(full_adder_7_out_5));
  full_adder full_adder_8 (
    .in_1(full_adder_7_out_5), .in_2(A[7]), .in_3(B[7]), .out_4(S[7]), .out_5(full_adder_8_out_5));
  full_adder full_adder_9 (
    .in_1(full_adder_8_out_5), .in_2(A[8]), .in_3(B[8]), .out_4(S[8]), .out_5(full_adder_9_out_5));
  full_adder full_adder_10 (
    .in_1(full_adder_9_out_5), .in_2(A[9]), .in_3(B[9]), .out_4(S[9]), .out_5(full_adder_10_out_5));
  full_adder full_adder_11 (
    .in_1(full_adder_10_out_5), .in_2(A[10]), .in_3(B[10]), .out_4(S[10]), .out_5(full_adder_11_out_5));
  full_adder full_adder_12 (.in_1(full_adder_11_out_5), .in_2(A[11]), .in_3(B[11]), .out_4(S[11]), .out_5(Cout));
endmodule

module _16bit_adder (
  input  [15:0] A,
  input  Cin,
  input  [15:0] B,
  output Cout,
  output [15:0] S
);

  wire full_adder_1_out_5, full_adder_2_out_5, full_adder_3_out_5, n12bit_adder_1_cout;

  _12bit_adder u_12bit_adder_1 (.A(A[11:0]), .B(B[11:0]), .Cout(n12bit_adder_1_cout), .S(S[11:0]), .Cin(Cin));
  full_adder full_adder_1 (
    .in_1(n12bit_adder_1_cout), .in_2(A[12]), .in_3(B[12]), .out_4(S[12]), .out_5(full_adder_1_out_5));
  full_adder full_adder_2 (
    .in_1(full_adder_1_out_5), .in_2(A[13]), .in_3(B[13]), .out_4(S[13]), .out_5(full_adder_2_out_5));
  full_adder full_adder_3 (
    .in_1(full_adder_2_out_5), .in_2(A[14]), .in_3(B[14]), .out_4(S[14]), .out_5(full_adder_3_out_5));
  full_adder full_adder_4 (.in_1(full_adder_3_out_5), .in_2(A[15]), .in_3(B[15]), .out_4(S[15]), .out_5(Cout));

  // Other names for the same wires on the sheet: a_t[11:0] = A[11:0]; b_t[11:0] = B[11:0]; s_t[11:0] = S[11:0]
endmodule
